// Digital circuit 8-Bit-Zählregister.dig as structural Verilog
module \_8_Bit_Zählregister  (
  input  [7:0] A_IN,
  input  INC,
  input  EN,
  input  CLK,
  input  RST,
  output [7:0] A_out
);

  wire [7:0] _8_bit_alu_1_p9, multiplexer_1_out;

  // _8_Bit_ALU _8_bit_alu_1: pin names not known; wires that end beside it: A_out, 8'h1, 1'b0, 1'b0, 1'b1, 1'b1, 1'b1, 1'b1, _8_bit_alu_1_p9
  Multiplexer #(.Bits(8)) multiplexer_1 (.sel(INC), .in_0(_8_bit_alu_1_p9), .in_1(A_IN), .out(multiplexer_1_out));
  // _8_Bit_Register _8_bit_register_1: pin names not known; wires that end beside it: multiplexer_1_out, EN, CLK, RST, A_out
endmodule
