// Digital circuit CompleteComputer.dig as structural Verilog
module CompleteComputer (
  input  CLK,
  input  RST,
  input  EN
);

  wire ALU_p5, and_1_out, c, not_1_out, steuerwerk_1_p1, steuerwerk_1_p4, steuerwerk_1_p5, steuerwerk_1_p6,
       steuerwerk_1_p7, steuerwerk_1_p8, steuerwerk_1_p9, steuerwerk_1_p10, steuerwerk_1_p11,
       steuerwerk_1_p12, steuerwerk_1_p13;
  wire [3:0] ALU_p3, ALU_p3_2;
  wire [7:0] AR_p3, IR_p5, multiplexer_1_out, PC_a_out;

  // Steuerwerk steuerwerk_1: pin names not known; wires that end beside it: steuerwerk_1_p1, c, RST, steuerwerk_1_p4, steuerwerk_1_p5, steuerwerk_1_p6, steuerwerk_1_p7, steuerwerk_1_p8, steuerwerk_1_p9, steuerwerk_1_p10, steuerwerk_1_p11, steuerwerk_1_p12, steuerwerk_1_p13
  and and_1 (and_1_out, CLK, EN);
  LED led_1 (.in(steuerwerk_1_p4));
  LED led_2 (.in(steuerwerk_1_p5));
  LED led_3 (.in(steuerwerk_1_p6));
  and and_2 (c, and_1_out, ~RST);  // And
  // Probe on steuerwerk_1_p1
  // _8_Bit_Register IR: pin names not known; wires that end beside it: RST, c, steuerwerk_1_p1, steuerwerk_1_p4, IR_p5
  // _8_Bit_Register AR: pin names not known; wires that end beside it: RST, c, AR_p3, steuerwerk_1_p5, IR_p5
  // Probe on AR_p3
  \_8_Bit_Zählregister  PC (
    .A_IN(AR_p3), .INC(steuerwerk_1_p10), .EN(steuerwerk_1_p11), .CLK(c), .RST(RST), .A_out(PC_a_out));
  // Probe on PC_a_out
  // Probe on PC_a_out
  // Probe on steuerwerk_1_p7
  // ALU_8Bit_Complete_Computer ALU: pin names not known; wires that end beside it: steuerwerk_1_p7, IR_p5, {ALU_p3_2, ALU_p3}, steuerwerk_1_p8, ALU_p5
  Multiplexer #(.Bits(8)) multiplexer_1 (
    .sel(steuerwerk_1_p12), .in_0(AR_p3), .in_1(PC_a_out), .out(multiplexer_1_out));
  // _8_Bit_Register Akku: pin names not known; wires that end beside it: ALU_p5, steuerwerk_1_p9, c, RST, {ALU_p3_2, ALU_p3}
  Seven_Seg_Hex seven_seg_hex_1 (.d(ALU_p3_2), .dp(1'b1));
  Seven_Seg_Hex seven_seg_hex_2 (.d(ALU_p3), .dp(1'b1));
  // Probe on {ALU_p3_2, ALU_p3}
  ROM #(.AddrBits(7), .Bits(8)) rom_1 (.A(multiplexer_1_out[6:0]), .sel(not_1_out), .D(IR_p5));
  not not_1 (not_1_out, multiplexer_1_out[7]);
  RAMDualPort #(.AddrBits(7), .Bits(8)) ramdualport_1 (
    .A(multiplexer_1_out[6:0]), .Din({ALU_p3_2, ALU_p3}), .str(steuerwerk_1_p13), .C(c),
    .ld(multiplexer_1_out[7]), .D(IR_p5));
  // Probe on IR_p5

  // Other names for the same wires on the sheet: r = RST

  // Notes on the sheet:
  //   CLK: Hz: 50
  //   contents of rom_1 (hex, n*v repeats v):
  //   18,0,1e,10,80,80,a0,2,0,0,0,0,0,0,0,0,1
endmodule
